// Logisim project 19101966_강민준.circ as structural Verilog: 8 circuits, main circuit decoder2
module decoder2 (
  input  Z,
  input  Y,
  input  X,
  input  W,
  output A,
  output B,
  output C,
  output D,
  output E,
  output F,
  output G
);

  wire and_1_out, and_2_out, and_3_out, and_4_out, G_out, not_1_out, not_2_out, not_3_out, or_1_out,
       or_2_out, or_3_out, xnor_1_out, xnor_2_out, xnor_3_out, xor_1_out, xor_2_out;

  not not_1 (not_1_out, X);
  not not_2 (not_2_out, Y);
  not not_3 (not_3_out, Z);
  and and_1 (and_1_out, not_3_out, X);
  xor xor_1 (xor_1_out, X, Y);
  and and_2 (and_2_out, not_2_out, not_3_out);
  xnor xnor_1 (xnor_1_out, X, Z);
  xnor xnor_2 (xnor_2_out, Y, Z);
  or or_1 (or_1_out, not_1_out, Y);
  or or_2 (or_2_out, W, not_2_out);
  xnor xnor_3 (xnor_3_out, X, Z);
  or or_3 (or_3_out, not_1_out, not_3_out);
  xor xor_2 (xor_2_out, W, Y);
  and and_3 (and_3_out, or_2_out, xnor_3_out);
  and and_4 (and_4_out, or_3_out, xor_2_out);
  or u_A (A, and_1_out, W, xor_1_out);
  or u_B (B, W, X, and_2_out);
  or u_C (C, W, Y, xnor_1_out);
  or u_D (D, W, not_1_out, xnor_2_out);
  and u_E (E, not_3_out, or_1_out);
  or u_F (F, and_3_out, and_4_out);
  and u_G (G_out, Y, not_3_out, not_1_out);
  not not_4 (G, G_out);
endmodule

module _10Counter (
  input  in_1,
  output out_2,
  output out_3,
  output out_4,
  output out_5,
  output out_6
);

  wire nand_1_out, not_1_out, not_2_out, not_3_out, not_4_out;

  T_Flip_Flop #(.trigger("falling")) t_ff_1 (
    .clk(in_1), .T(1'b1), .Q(out_2), .reset(not_1_out));  // open: Qn, preset, en
  not not_1 (not_1_out, nand_1_out);
  T_Flip_Flop #(.trigger("falling")) t_ff_2 (
    .clk(out_2), .T(1'b1), .Q(out_3), .reset(not_2_out));  // open: Qn, preset, en
  not not_2 (not_2_out, nand_1_out);
  not not_3 (not_3_out, nand_1_out);
  T_Flip_Flop #(.trigger("falling")) t_ff_3 (
    .clk(out_3), .T(1'b1), .Q(out_4), .reset(not_3_out));  // open: Qn, preset, en
  T_Flip_Flop #(.trigger("falling")) t_ff_4 (
    .clk(out_4), .T(1'b1), .Q(out_5), .reset(not_4_out));  // open: Qn, preset, en
  not not_4 (not_4_out, nand_1_out);
  nand nand_1 (nand_1_out, out_3, out_5);

  assign out_6 = out_5;
endmodule

module _6Counter (
  input  in_1,
  output out_2,
  output out_3,
  output out_4,
  output out_5,
  output out_6
);

  wire nand_1_out, not_1_out, not_2_out, not_3_out, not_4_out;

  T_Flip_Flop #(.trigger("falling")) t_ff_1 (
    .clk(in_1), .T(1'b1), .Q(out_2), .reset(not_1_out));  // open: Qn, preset, en
  not not_1 (not_1_out, nand_1_out);
  T_Flip_Flop #(.trigger("falling")) t_ff_2 (
    .clk(out_2), .T(1'b1), .Q(out_3), .reset(not_2_out));  // open: Qn, preset, en
  not not_2 (not_2_out, nand_1_out);
  T_Flip_Flop #(.trigger("falling")) t_ff_3 (
    .clk(out_3), .T(1'b1), .Q(out_4), .reset(not_3_out));  // open: Qn, preset, en
  not not_3 (not_3_out, nand_1_out);
  T_Flip_Flop #(.trigger("falling")) t_ff_4 (
    .clk(out_4), .T(1'b1), .Q(out_5), .reset(not_4_out));  // open: Qn, preset, en
  not not_4 (not_4_out, nand_1_out);
  nand nand_1 (nand_1_out, out_4, out_3);

  assign out_6 = out_4;
endmodule

module test (
  input  in_1,
  input  in_2,
  input  in_3,
  input  in_4,
  input  in_5,
  input  in_6
);

  wire decoder2_1_a, decoder2_1_b, decoder2_1_c, decoder2_1_d, decoder2_1_e, decoder2_1_f, decoder2_1_g,
       decoder2_2_a, decoder2_2_b, decoder2_2_c, decoder2_2_d, decoder2_2_e, decoder2_2_f, decoder2_2_g,
       decoder2_3_a, decoder2_3_b, decoder2_3_c, decoder2_3_d, decoder2_3_e, decoder2_3_f, decoder2_3_g,
       decoder2_4_a, decoder2_4_b, decoder2_4_c, decoder2_4_d, decoder2_4_e, decoder2_4_f, decoder2_4_g,
       decoder2_5_a, decoder2_5_b, decoder2_5_c, decoder2_5_d, decoder2_5_e, decoder2_5_f, decoder2_5_g,
       decoder2_6_a, decoder2_6_b, decoder2_6_c, decoder2_6_d, decoder2_6_e, decoder2_6_f, decoder2_6_g,
       n6counter_1_out_2, n6counter_1_out_3, n6counter_1_out_4, n6counter_1_out_5, n6counter_1_out_6,
       n6counter_2_out_2, n6counter_2_out_3, n6counter_2_out_4, n6counter_2_out_5, n6counter_2_out_6,
       n10counter_1_out_2, n10counter_1_out_3, n10counter_1_out_4, n10counter_1_out_5, n10counter_1_out_6,
       n10counter_24_1_out_2, n10counter_24_1_out_3, n10counter_24_1_out_4, n10counter_24_1_out_5,
       n10counter_24_1_out_6, n10counter_24_1_out_7, n10counter_24_1_out_8, n10counter_24_1_out_9,
       n10counter_not_1_out_2, n10counter_not_1_out_3, n10counter_not_1_out_4, n10counter_not_1_out_5,
       n10counter_not_1_out_6;

  decoder2 decoder2_1 (
    .Z(n10counter_24_1_out_6), .Y(n10counter_24_1_out_7), .X(n10counter_24_1_out_8),
    .W(n10counter_24_1_out_9), .A(decoder2_1_a), .B(decoder2_1_b), .C(decoder2_1_c), .D(decoder2_1_d),
    .E(decoder2_1_e), .F(decoder2_1_f), .G(decoder2_1_g));
  _7_Segment_Display u_7_segment_display_1 (
    .g(decoder2_1_a), .f(decoder2_1_b), .a(decoder2_1_c), .b(decoder2_1_d), .e(decoder2_1_e),
    .d(decoder2_1_f), .c(decoder2_1_g));  // open: dp
  decoder2 decoder2_2 (
    .Z(n10counter_24_1_out_2), .Y(n10counter_24_1_out_3), .X(n10counter_24_1_out_4),
    .W(n10counter_24_1_out_5), .A(decoder2_2_a), .B(decoder2_2_b), .C(decoder2_2_c), .D(decoder2_2_d),
    .E(decoder2_2_e), .F(decoder2_2_f), .G(decoder2_2_g));
  _10Counter_24 u_10counter_24_1 (
    .in_1(n6counter_1_out_6), .out_6(n10counter_24_1_out_6), .out_7(n10counter_24_1_out_7),
    .out_8(n10counter_24_1_out_8), .out_9(n10counter_24_1_out_9), .out_2(n10counter_24_1_out_2),
    .out_3(n10counter_24_1_out_3), .out_4(n10counter_24_1_out_4), .out_5(n10counter_24_1_out_5));
  _7_Segment_Display u_7_segment_display_2 (
    .g(decoder2_2_a), .f(decoder2_2_b), .a(decoder2_2_c), .b(decoder2_2_d), .e(decoder2_2_e),
    .d(decoder2_2_f), .c(decoder2_2_g));  // open: dp
  decoder2 decoder2_3 (
    .Z(n6counter_1_out_2), .Y(n6counter_1_out_3), .X(n6counter_1_out_4), .W(n6counter_1_out_5),
    .A(decoder2_3_a), .B(decoder2_3_b), .C(decoder2_3_c), .D(decoder2_3_d), .E(decoder2_3_e),
    .F(decoder2_3_f), .G(decoder2_3_g));
  _7_Segment_Display u_7_segment_display_3 (
    .g(decoder2_3_a), .f(decoder2_3_b), .a(decoder2_3_c), .b(decoder2_3_d), .e(decoder2_3_e),
    .d(decoder2_3_f), .c(decoder2_3_g));  // open: dp
  _6Counter u_6counter_1 (
    .in_1(n10counter_not_1_out_6), .out_2(n6counter_1_out_2), .out_3(n6counter_1_out_3),
    .out_4(n6counter_1_out_4), .out_5(n6counter_1_out_5), .out_6(n6counter_1_out_6));
  _7_Segment_Display u_7_segment_display_4 (
    .g(decoder2_4_a), .f(decoder2_4_b), .a(decoder2_4_c), .b(decoder2_4_d), .e(decoder2_4_e),
    .d(decoder2_4_f), .c(decoder2_4_g));  // open: dp
  decoder2 decoder2_4 (
    .Z(n10counter_not_1_out_2), .Y(n10counter_not_1_out_3), .X(n10counter_not_1_out_4),
    .W(n10counter_not_1_out_5), .A(decoder2_4_a), .B(decoder2_4_b), .C(decoder2_4_c), .D(decoder2_4_d),
    .E(decoder2_4_e), .F(decoder2_4_f), .G(decoder2_4_g));
  _10Counter_NOT u_10counter_not_1 (
    .in_1(n6counter_2_out_6), .out_2(n10counter_not_1_out_2), .out_3(n10counter_not_1_out_3),
    .out_4(n10counter_not_1_out_4), .out_5(n10counter_not_1_out_5), .out_6(n10counter_not_1_out_6));
  decoder2 decoder2_5 (
    .Z(n6counter_2_out_2), .Y(n6counter_2_out_3), .X(n6counter_2_out_4), .W(n6counter_2_out_5),
    .A(decoder2_5_a), .B(decoder2_5_b), .C(decoder2_5_c), .D(decoder2_5_d), .E(decoder2_5_e),
    .F(decoder2_5_f), .G(decoder2_5_g));
  _7_Segment_Display u_7_segment_display_5 (
    .g(decoder2_5_a), .f(decoder2_5_b), .a(decoder2_5_c), .b(decoder2_5_d), .e(decoder2_5_e),
    .d(decoder2_5_f), .c(decoder2_5_g));  // open: dp
  decoder2 decoder2_6 (
    .Z(n10counter_1_out_2), .Y(n10counter_1_out_3), .X(n10counter_1_out_4), .W(n10counter_1_out_5),
    .A(decoder2_6_a), .B(decoder2_6_b), .C(decoder2_6_c), .D(decoder2_6_d), .E(decoder2_6_e),
    .F(decoder2_6_f), .G(decoder2_6_g));
  _6Counter u_6counter_2 (
    .in_1(n10counter_1_out_6), .out_2(n6counter_2_out_2), .out_3(n6counter_2_out_3),
    .out_4(n6counter_2_out_4), .out_5(n6counter_2_out_5), .out_6(n6counter_2_out_6));
  _7_Segment_Display u_7_segment_display_6 (
    .g(decoder2_6_a), .f(decoder2_6_b), .a(decoder2_6_c), .b(decoder2_6_d), .e(decoder2_6_e),
    .d(decoder2_6_f), .c(decoder2_6_g));  // open: dp
  _10Counter u_10counter_1 (
    .out_2(n10counter_1_out_2), .out_3(n10counter_1_out_3), .out_4(n10counter_1_out_4),
    .out_5(n10counter_1_out_5), .out_6(n10counter_1_out_6));  // open: in_1
endmodule

module _10Counter_NOT (
  input  in_1,
  output out_2,
  output out_3,
  output out_4,
  output out_5,
  output out_6
);

  wire nand_1_out, not_1_out, not_2_out, not_3_out, not_4_out;

  T_Flip_Flop #(.trigger("falling")) t_ff_1 (
    .clk(in_1), .T(1'b1), .Q(out_2), .reset(not_1_out));  // open: Qn, preset, en
  not not_1 (not_1_out, nand_1_out);
  T_Flip_Flop #(.trigger("falling")) t_ff_2 (
    .clk(out_2), .T(1'b1), .Q(out_3), .reset(not_2_out));  // open: Qn, preset, en
  not not_2 (not_2_out, nand_1_out);
  not not_3 (not_3_out, nand_1_out);
  T_Flip_Flop #(.trigger("falling")) t_ff_3 (
    .clk(out_3), .T(1'b1), .Q(out_4), .reset(not_3_out));  // open: Qn, preset, en
  T_Flip_Flop #(.trigger("falling")) t_ff_4 (
    .clk(out_4), .T(1'b1), .Q(out_5), .reset(not_4_out));  // open: Qn, preset, en
  not not_4 (not_4_out, nand_1_out);
  nand nand_1 (nand_1_out, out_3, out_5);

  assign out_6 = out_5;
endmodule

module _3Counter (
  input  in_1,
  output out_2,
  output out_3,
  output out_4,
  output out_5,
  output out_6
);

  wire nand_1_out, not_1_out, not_2_out, not_3_out, not_4_out;

  T_Flip_Flop #(.trigger("falling")) t_ff_1 (
    .clk(in_1), .T(1'b1), .Q(out_2), .reset(not_1_out));  // open: Qn, preset, en
  not not_1 (not_1_out, nand_1_out);
  T_Flip_Flop #(.trigger("falling")) t_ff_2 (
    .clk(out_2), .T(1'b1), .Q(out_3), .reset(not_2_out));  // open: Qn, preset, en
  not not_2 (not_2_out, nand_1_out);
  T_Flip_Flop #(.trigger("falling")) t_ff_3 (
    .clk(out_3), .T(1'b1), .Q(out_4), .reset(not_3_out));  // open: Qn, preset, en
  not not_3 (not_3_out, nand_1_out);
  T_Flip_Flop #(.trigger("falling")) t_ff_4 (
    .clk(out_4), .T(1'b1), .Q(out_5), .reset(not_4_out));  // open: Qn, preset, en
  not not_4 (not_4_out, nand_1_out);
  nand nand_1 (nand_1_out, out_3, out_2);

  assign out_6 = out_3;
endmodule

module _10Counter_24 (
  input  in_1,
  output out_2,
  output out_3,
  output out_4,
  output out_5,
  output out_6,
  output out_7,
  output out_8,
  output out_9
);

  wire nand_1_out, nand_2_out, not_1_out, not_2_out, not_3_out, not_4_out, not_5_out, not_6_out, not_7_out,
       not_8_out, not_9_out, not_10_out, not_11_out, not_12_out, or_1_out, or_2_out, or_3_out, or_4_out;

  T_Flip_Flop #(.trigger("falling")) t_ff_1 (
    .clk(out_5), .T(1'b1), .Q(out_6), .reset(not_1_out));  // open: Qn, preset, en
  not not_1 (not_1_out, nand_1_out);
  T_Flip_Flop #(.trigger("falling")) t_ff_2 (
    .clk(out_6), .T(1'b1), .Q(out_7), .reset(not_2_out));  // open: Qn, preset, en
  not not_2 (not_2_out, nand_1_out);
  T_Flip_Flop #(.trigger("falling")) t_ff_3 (
    .clk(out_7), .T(1'b1), .Q(out_8), .reset(not_3_out));  // open: Qn, preset, en
  not not_3 (not_3_out, nand_1_out);
  T_Flip_Flop #(.trigger("falling")) t_ff_4 (
    .clk(out_8), .T(1'b1), .Q(out_9), .reset(not_4_out));  // open: Qn, preset, en
  not not_4 (not_4_out, nand_1_out);
  nand nand_1 (nand_1_out, out_7, out_4);
  T_Flip_Flop #(.trigger("falling")) t_ff_5 (
    .clk(in_1), .T(1'b1), .Q(out_2), .reset(or_1_out));  // open: Qn, preset, en
  or or_1 (or_1_out, not_6_out, not_5_out);
  not not_5 (not_5_out, nand_2_out);
  not not_6 (not_6_out, nand_1_out);
  T_Flip_Flop #(.trigger("falling")) t_ff_6 (
    .clk(out_2), .T(1'b1), .Q(out_3), .reset(or_2_out));  // open: Qn, preset, en
  or or_2 (or_2_out, not_8_out, not_7_out);
  not not_7 (not_7_out, nand_2_out);
  not not_8 (not_8_out, nand_1_out);
  or or_3 (or_3_out, not_9_out, not_10_out);
  not not_9 (not_9_out, nand_1_out);
  T_Flip_Flop #(.trigger("falling")) t_ff_7 (
    .clk(out_3), .T(1'b1), .Q(out_4), .reset(or_3_out));  // open: Qn, preset, en
  not not_10 (not_10_out, nand_2_out);
  T_Flip_Flop #(.trigger("falling")) t_ff_8 (
    .clk(out_4), .T(1'b1), .Q(out_5), .reset(or_4_out));  // open: Qn, preset, en
  or or_4 (or_4_out, not_12_out, not_11_out);
  nand nand_2 (nand_2_out, out_5, out_3);
  not not_11 (not_11_out, nand_2_out);
  not not_12 (not_12_out, nand_1_out);
endmodule

module Main (
);

  wire clock_1_out, decoder2_1_a, decoder2_1_b, decoder2_1_c, decoder2_1_d, decoder2_1_e, decoder2_1_f,
       decoder2_1_g, decoder2_2_a, decoder2_2_b, decoder2_2_c, decoder2_2_d, decoder2_2_e, decoder2_2_f,
       decoder2_2_g, decoder2_3_a, decoder2_3_b, decoder2_3_c, decoder2_3_d, decoder2_3_e, decoder2_3_f,
       decoder2_3_g, decoder2_4_a, decoder2_4_b, decoder2_4_c, decoder2_4_d, decoder2_4_e, decoder2_4_f,
       decoder2_4_g, decoder2_5_a, decoder2_5_b, decoder2_5_c, decoder2_5_d, decoder2_5_e, decoder2_5_f,
       decoder2_5_g, decoder2_6_a, decoder2_6_b, decoder2_6_c, decoder2_6_d, decoder2_6_e, decoder2_6_f,
       decoder2_6_g, n6counter_1_out_2, n6counter_1_out_3, n6counter_1_out_4, n6counter_1_out_5,
       n6counter_1_out_6, n6counter_2_out_2, n6counter_2_out_3, n6counter_2_out_4, n6counter_2_out_5,
       n6counter_2_out_6, n10counter_1_out_2, n10counter_1_out_3, n10counter_1_out_4, n10counter_1_out_5,
       n10counter_1_out_6, n10counter_24_1_out_2, n10counter_24_1_out_3, n10counter_24_1_out_4,
       n10counter_24_1_out_5, n10counter_24_1_out_6, n10counter_24_1_out_7, n10counter_24_1_out_8,
       n10counter_24_1_out_9, n10counter_not_1_out_2, n10counter_not_1_out_3, n10counter_not_1_out_4,
       n10counter_not_1_out_5, n10counter_not_1_out_6;

  decoder2 decoder2_1 (
    .Z(n10counter_24_1_out_6), .Y(n10counter_24_1_out_7), .X(n10counter_24_1_out_8),
    .W(n10counter_24_1_out_9), .A(decoder2_1_a), .B(decoder2_1_b), .C(decoder2_1_c), .D(decoder2_1_d),
    .E(decoder2_1_e), .F(decoder2_1_f), .G(decoder2_1_g));
  _7_Segment_Display u_7_segment_display_1 (
    .g(decoder2_1_a), .f(decoder2_1_b), .a(decoder2_1_c), .b(decoder2_1_d), .e(decoder2_1_e),
    .d(decoder2_1_f), .c(decoder2_1_g));  // open: dp
  decoder2 decoder2_2 (
    .Z(n10counter_24_1_out_2), .Y(n10counter_24_1_out_3), .X(n10counter_24_1_out_4),
    .W(n10counter_24_1_out_5), .A(decoder2_2_a), .B(decoder2_2_b), .C(decoder2_2_c), .D(decoder2_2_d),
    .E(decoder2_2_e), .F(decoder2_2_f), .G(decoder2_2_g));
  _10Counter_24 u_10counter_24_1 (
    .in_1(n6counter_1_out_6), .out_6(n10counter_24_1_out_6), .out_7(n10counter_24_1_out_7),
    .out_8(n10counter_24_1_out_8), .out_9(n10counter_24_1_out_9), .out_2(n10counter_24_1_out_2),
    .out_3(n10counter_24_1_out_3), .out_4(n10counter_24_1_out_4), .out_5(n10counter_24_1_out_5));
  _7_Segment_Display u_7_segment_display_2 (
    .g(decoder2_2_a), .f(decoder2_2_b), .a(decoder2_2_c), .b(decoder2_2_d), .e(decoder2_2_e),
    .d(decoder2_2_f), .c(decoder2_2_g));  // open: dp
  decoder2 decoder2_3 (
    .Z(n6counter_1_out_2), .Y(n6counter_1_out_3), .X(n6counter_1_out_4), .W(n6counter_1_out_5),
    .A(decoder2_3_a), .B(decoder2_3_b), .C(decoder2_3_c), .D(decoder2_3_d), .E(decoder2_3_e),
    .F(decoder2_3_f), .G(decoder2_3_g));
  _7_Segment_Display u_7_segment_display_3 (
    .g(decoder2_3_a), .f(decoder2_3_b), .a(decoder2_3_c), .b(decoder2_3_d), .e(decoder2_3_e),
    .d(decoder2_3_f), .c(decoder2_3_g));  // open: dp
  _6Counter u_6counter_1 (
    .in_1(n10counter_not_1_out_6), .out_2(n6counter_1_out_2), .out_3(n6counter_1_out_3),
    .out_4(n6counter_1_out_4), .out_5(n6counter_1_out_5), .out_6(n6counter_1_out_6));
  _7_Segment_Display u_7_segment_display_4 (
    .g(decoder2_4_a), .f(decoder2_4_b), .a(decoder2_4_c), .b(decoder2_4_d), .e(decoder2_4_e),
    .d(decoder2_4_f), .c(decoder2_4_g));  // open: dp
  decoder2 decoder2_4 (
    .Z(n10counter_not_1_out_2), .Y(n10counter_not_1_out_3), .X(n10counter_not_1_out_4),
    .W(n10counter_not_1_out_5), .A(decoder2_4_a), .B(decoder2_4_b), .C(decoder2_4_c), .D(decoder2_4_d),
    .E(decoder2_4_e), .F(decoder2_4_f), .G(decoder2_4_g));
  _10Counter_NOT u_10counter_not_1 (
    .in_1(n6counter_2_out_6), .out_2(n10counter_not_1_out_2), .out_3(n10counter_not_1_out_3),
    .out_4(n10counter_not_1_out_4), .out_5(n10counter_not_1_out_5), .out_6(n10counter_not_1_out_6));
  decoder2 decoder2_5 (
    .Z(n6counter_2_out_2), .Y(n6counter_2_out_3), .X(n6counter_2_out_4), .W(n6counter_2_out_5),
    .A(decoder2_5_a), .B(decoder2_5_b), .C(decoder2_5_c), .D(decoder2_5_d), .E(decoder2_5_e),
    .F(decoder2_5_f), .G(decoder2_5_g));
  _7_Segment_Display u_7_segment_display_5 (
    .g(decoder2_5_a), .f(decoder2_5_b), .a(decoder2_5_c), .b(decoder2_5_d), .e(decoder2_5_e),
    .d(decoder2_5_f), .c(decoder2_5_g));  // open: dp
  decoder2 decoder2_6 (
    .Z(n10counter_1_out_2), .Y(n10counter_1_out_3), .X(n10counter_1_out_4), .W(n10counter_1_out_5),
    .A(decoder2_6_a), .B(decoder2_6_b), .C(decoder2_6_c), .D(decoder2_6_d), .E(decoder2_6_e),
    .F(decoder2_6_f), .G(decoder2_6_g));
  _6Counter u_6counter_2 (
    .in_1(n10counter_1_out_6), .out_2(n6counter_2_out_2), .out_3(n6counter_2_out_3),
    .out_4(n6counter_2_out_4), .out_5(n6counter_2_out_5), .out_6(n6counter_2_out_6));
  _7_Segment_Display u_7_segment_display_6 (
    .g(decoder2_6_a), .f(decoder2_6_b), .a(decoder2_6_c), .b(decoder2_6_d), .e(decoder2_6_e),
    .d(decoder2_6_f), .c(decoder2_6_g));  // open: dp
  _10Counter u_10counter_1 (
    .in_1(clock_1_out), .out_2(n10counter_1_out_2), .out_3(n10counter_1_out_3), .out_4(n10counter_1_out_4),
    .out_5(n10counter_1_out_5), .out_6(n10counter_1_out_6));
  Clock clock_1 (.out(clock_1_out));
endmodule
